# Fritzing sketch breadnbutter-lm386-filled (saved by Fritzing 1.0.3b)
circuit board: 4.99999cm x 10cm
breadboards: 2

parts:
  S11 = SPST Switch [package=switch-spdt_kit]
  Power_plug2 = Power plug
  4001 = Rectifier Diode [part_number=1N4001 package="300 mil [THT]"]
  100uF = Electrolytic Capacitor [capacitance=0.1mF voltage=35V package="100 mil [THT, electrolytic]"]
  LM7805 = Voltage Regulator [package=to220-igo]
  100uF1 = Electrolytic Capacitor [capacitance=0.1mF voltage=35V package="100 mil [THT, electrolytic]"]
  104 = Ceramic Capacitor [capacitance=100nF voltage=16V package="200 mil [THT, multilayer]"]
  -G = double row female pin header, 4 pins [form="♀ (female)"]
  +v = double row female pin header, 4 pins [form="♀ (female)"]
  +5v = double row female pin header, 4 pins [form="♀ (female)"]
  J4 = double row female pin header, 2 pins [form="♀ (female)"]
  LED2 = LED - 3mm [color="Blue (505nm)" current=0.030A package="3 mm [THT]"]
  1K = Resistor [tolerance=±5% resistance=1k power=0.25W package=THT]
  LED3 = LED - 3mm [color="Blue (505nm)" current=0.030A package="3 mm [THT]"]
  1K_2 = Resistor [tolerance=±5% resistance=1k power=0.25W package=THT]
  Input = Audio Jack (TRS) 3.5mm [package="PG203J [THT]"]
  input = double row female pin header, 4 pins [form="♀ (female)"]
  LDR = double row female pin header, 4 pins [form="♀ (female)"]
  LED4 = LED - 3mm [color="Red (635nm)" current=0.030A package="3 mm [THT]"]
  1K1 = Resistor [tolerance=±5% resistance=1k power=0.25W package=THT]
  LDR1 = Photocell (LDR) [power=0.25W dark_resistance_@0.01lx=300kΩ light_resistance_@100lx=400Ω luminance=10lx package=THT]
  LED = female pin header, 2 pins [form="♀ (female)"]
  100K = Rotary Potentiometer (Small) [maximum_resistance=100kΩ knob_status=50% power=0.5W package=THT]
  Jm2 = double row female pin header, 6 pins [form="♀ (female)"]
  100K_2 = Rotary Potentiometer (Small) [maximum_resistance=100kΩ knob_status=50% power=0.5W package=THT]
  100K_3 = Rotary Potentiometer (Small) [maximum_resistance=100kΩ knob_status=50% power=0.5W package=THT]
  Jm4 = double row female pin header, 6 pins [form="♀ (female)"]
  100K_4 = Rotary Potentiometer (Small) [maximum_resistance=100kΩ knob_status=50% power=0.5W package=THT]
  Jm5 = double row female pin header, 6 pins [form="♀ (female)"]
  Jm6 = double row female pin header, 6 pins [form="♀ (female)"]
  out = Audio Jack (TRS) 3.5mm [package="PG203J [THT]"]
  1-10K = Rotary Potentiometer (Small) [maximum_resistance=10kΩ knob_status=50% power=0.5W package=THT]
  10K = Resistor [tolerance=±5% resistance=10k power=0.25W package=THT]
  47pf = Ceramic Capacitor [capacitance=47pF voltage=16V package="200 mil [THT, multilayer]"]
  out_2 = double row female pin header, 2 pins [form="♀ (female)"]
  100u = Electrolytic Capacitor [capacitance=0.1mF voltage=35V package="100 mil [THT, electrolytic]"]
  104_2 = Ceramic Capacitor [capacitance=100nF voltage=16V package="200 mil [THT, multilayer]"]
  10 = Resistor [tolerance=±5% resistance=10 power=0.25W package=THT]
  SPKR = Loudspeaker
  sw2 = SPST Switch [package=switch-spdt_kit]
  sw1 = SPST Switch [package=switch-spdt_kit]
  sw1_2 = female pin header, 2 pins [form="♀ (female)"]
  sw2_2 = female pin header, 2 pins [form="♀ (female)"]
  LM386 = LM386 [package=dip08]
  10u = Electrolytic Capacitor [capacitance=10µF voltage=35V package="100 mil [THT, electrolytic]"]
  10u_2 = Electrolytic Capacitor [capacitance=10µF voltage=35V package="100 mil [THT, electrolytic]"]
  AMP = double row female pin header, 4 pins [form="♀ (female)"]
  105 = Ceramic Capacitor [capacitance=1µF voltage=16V package="200 mil [THT, multilayer]"]
  Touch = TOUCH [package=touch1]
  sw3 = female pin header, 2 pins [form="♀ (female)"]
  touch = female pin header, 2 pins [form="♀ (female)"]
  LED2_2 = female pin header, 2 pins [form="♀ (female)"]
  LED6 = LED - 3mm [color="Red (635nm)" current=0.030A package="3 mm [THT]"]
  1K2 = Resistor [tolerance=±5% resistance=1k power=0.25W package=THT]
  LDR2 = double row female pin header, 4 pins [form="♀ (female)"]
  LDR3 = Photocell (LDR) [power=0.25W dark_resistance_@0.01lx=300kΩ light_resistance_@100lx=400Ω luminance=10lx package=THT]
  LED7 = female pin header, 1 pin [form="♀ (female)"]
  LED8 = female pin header, 1 pin [form="♀ (female)"]
  LED9 = female pin header, 1 pin [form="♀ (female)"]
  104_3 = Ceramic Capacitor [capacitance=100nF voltage=16V package="200 mil [THT, multilayer]"]
  l = female pin header, 1 pin [form="♀ (female)"]  # not connected
  10K_2 = Rotary Potentiometer (Small) [maximum_resistance=10kΩ knob_status=50% power=0.5W package=THT]

nets:
  N1: S11.O, LED9.pin1
  N2: S11.P, Power_plug2.VCC, J4.pin1
  N3: S11.S, 4001.anode
  GND: Power_plug2.GND, 100uF.-, LM7805.GND, 100uF1.-, 104.1, -G.pin1, -G.pin2, -G.pin3, -G.pin4, J4.pin2, 1K.Pin_1, 1K_2.Pin_1, Input.Sleeve, 1K1.Pin_1, out.Sleeve, 1-10K.leg1, 47pf.0, 47pf.1, out_2.pin1, 10.Pin_1, SPKR.pin2, LM386.-IN, LM386.V-, 10u_2.-, 1K2.Pin_1, 104_3.1, 10K_2.leg1
  N4: 4001.cathode, 100uF.+, LM7805.IN, +v.pin1, +v.pin2, +v.pin3, +v.pin4, LED3.anode, LM386.V+, 104_3.0
  N5: LM7805.OUT, 100uF1.+, 104.0, +5v.pin1, +5v.pin2, +5v.pin3, +5v.pin4, LED2.anode
  N6: LED2.cathode, 1K.Pin_0
  N7: LED3.cathode, 1K_2.Pin_0
  N8: Input.Ring, input.pin3, input.pin4
  N9: Input.Tip, input.pin1, input.pin2
  N10: LDR.pin1, LDR.pin2, LDR1.pin_1
  N11: LDR.pin3, LDR.pin4, LDR1.pin_0
  N12: LED4.cathode, 1K1.Pin_0
  N13: LED4.anode, LED.pin1, LED.pin2
  N14: 100K.leg1, Jm2.pin3, Jm2.pin4
  N15: 100K.wiper, Jm2.pin2, Jm2.pin5
  N16: 100K.leg2, Jm2.pin1, Jm2.pin6
  N17: 100K_2.leg1, Jm6.pin3, Jm6.pin4
  N18: 100K_2.wiper, Jm6.pin2, Jm6.pin5
  N19: 100K_2.leg2, Jm6.pin1, Jm6.pin6
  N20: 100K_3.leg1, Jm4.pin3, Jm4.pin4
  N21: 100K_3.wiper, Jm4.pin2, Jm4.pin5
  N22: 100K_3.leg2, Jm4.pin1, Jm4.pin6
  N23: 100K_4.leg1, Jm5.pin3, Jm5.pin4
  N24: 100K_4.wiper, Jm5.pin2, Jm5.pin5
  N25: 100K_4.leg2, Jm5.pin1, Jm5.pin6
  N26: out.Ring, out.Tip, out_2.pin2, 100u.-, SPKR.pin1
  N27: 1-10K.wiper, LM386.+IN
  N28: 1-10K.leg2, AMP.pin3, AMP.pin4, 105.1
  N29: 10K.Pin_0, LM386.BP
  N30: 10K.Pin_1, 10u_2.+
  N31: 100u.+, 104_2.1, LM386.OUT
  N32: 104_2.0, 10.Pin_0
  N33: sw2.O, sw2_2.pin1
  N34: sw2.P, sw2_2.pin2
  N35: sw2.S, LED7.pin1
  N36: sw1.O, sw1_2.pin1
  N37: sw1.P, sw1_2.pin2
  N38: sw1.S, LED8.pin1
  N39: LM386.GAIN, 10u.-, 10K_2.wiper
  N40: 10u.+, 10K_2.leg2
  N41: AMP.pin1, AMP.pin2, 105.0
  N42: Touch.T1, touch.pin1, touch.pin2
  N43: Touch.T2, sw3.pin1, sw3.pin2
  N44: LED2_2.pin1, LED2_2.pin2, LED6.anode
  N45: LED6.cathode, 1K2.Pin_0
  N46: LDR2.pin1, LDR2.pin2, LDR3.pin_1
  N47: LDR2.pin3, LDR2.pin4, LDR3.pin_0

notes:
  bread'n'butter
  blueprint@poetaster.de 2024
  jlcjlcjlcjlc
